# Fritzing sketch scheme (saved by Fritzing 0.9.5d)

parts:
  R1 = Resistor [tolerance=±5% resistance=1500 package=THT]
  S1 = Round Pushbutton
  U1 = WS2812 RGB LED strip
  Компонент2 = Adafruit MAX4466 Electret Microphone Amplifier [part_number="Adafruit #1063"]
  Power_5_5x2_1 = Power 5.5x2.5
  R2 = Resistor [tolerance=±5% resistance=330 package=THT]
  Компонент1 = Arduino Nano (Rev3.0) (ICSP)

nets:
  N1: R1.Pin_0, S1.leg0, Компонент1.D3
  GND: R1.Pin_1, U1.GND, Компонент2.GND, Power_5_5x2_1.GND, Компонент1.GND
  VCC: S1.leg1, U1.VCC, Power_5_5x2_1.PWR, Компонент1.5V
  N2: U1.DIN, R2.Pin_1
  VCC_2: Компонент2.VCC, Компонент1.3V3
  N3: Компонент2.OUT, Компонент1.A0
  N4: R2.Pin_0, Компонент1.D2

custom parts:
  WS2812 RGB LED strip: WS2812 strip
  Adafruit MAX4466 Electret Microphone Amplifier: Add an ear to your project with this well-designed electret microphone amplifier. This fully assembled and tested board comes with a 20-20KHz electret microphone soldered on. For the amplification, we use the Maxim MAX4466, an op-amp specifically designed for this delicate task! The amplifier has excellent power supply noise rejection, so this amplifier sounds really good and isn't nearly as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
